// Logisim project Lab_2_ECE_255_AS.circ as structural Verilog
module main (
  input  x2,
  input  x1,
  input  x0
);

  wire adder_1_cout, adder_1_out, adder_2_cout, adder_2_out, adder_3_cout, adder_3_out;

  Adder #(.width(1)) adder_1 (.a(x2), .b(1'b0), .out(adder_1_out), .cin(adder_2_cout), .cout(adder_1_cout));
  Adder #(.width(1)) adder_2 (.a(1'b0), .b(x1), .out(adder_2_out), .cin(adder_3_cout), .cout(adder_2_cout));
  Adder #(.width(1)) adder_3 (.a(x0), .b(1'b1), .out(adder_3_out), .cin(1'b0), .cout(adder_3_cout));
  LED led_1 (.in(adder_1_cout));
  LED led_2 (.in(adder_1_out));
  LED led_3 (.in(adder_2_out));
  LED led_4 (.in(adder_3_out));
endmodule
